# Fritzing sketch temperature variation control (saved by Fritzing 0.9.3b)
breadboards: 1

parts:
  AT_MEGA_328 = Arduino Uno (Rev3)
  T1 = LM35 Temperature Sensor [package="TO92 [THT]"]
  RELAY = RELAY [package=relay-t9a]
  L1 = Inductor [package="1206 [SMD]"]
  220V_AC = Power plug
  FAN = LilyPad Buzzer

nets (from the breadboard view):
  N1: AT_MEGA_328.A0, T1.Vout
  N2: AT_MEGA_328.D8, RELAY.COIL1
  GND: AT_MEGA_328.GND, T1.GND, RELAY.COIL2, FAN.-
  N3: AT_MEGA_328.D7, FAN.+
  N4: AT_MEGA_328.5V, T1.+Vs
  N5: RELAY.MAIN, 220V_AC.VCC
  N6: RELAY.NO, L1.pin_0
  N7: L1.pin_1, 220V_AC.GND

// code stored in the sketch: temperature variation control.ino

int sensor=A0; //sensor is connected to A0 analog pin
int fan=8;// fan is connected to 8 digital pin
int relay=7;// relay IN pin connected to 7 digital pin
void setup() {
 pinMode(sensor,INPUT);
 pinMode(fan,OUTPUT);
 pinMode(relay,OUTPUT);
 Serial.begin(9600);
}

void loop() {
    // measure the temperature and store it in a variable called "temp"

  int temp = analogRead(A0);  // assuming the temperature sensor is connected to analog pin A0
  // convert the analog reading to voltage
  float voltage = temp * 5.0 / 1023.0;
    // convert the voltage to temperature in degrees Celsius
  float celsius = (voltage ) * 100.0;
    // display the temperature on the Serial monitor
 Serial.print("\n");
 Serial.print("TEMPERATURE=");// print the text "Temperature:"
Serial.print(celsius);// print the temperature in degrees Celsius
Serial.print("*C");// print the unit "C" for Celsius

if(celsius>30)
{
  digitalWrite(fan,HIGH);//fan will be ON if temperature vary above 25 deg cel
  digitalWrite(relay,LOW);// relay IN pin LOW
}
else
{
    digitalWrite(fan,LOW);//fan will be OFF if temperature is  equal or below 25 deg cel
    digitalWrite(relay,HIGH);// relay IN pin will give signal which will connect COM and NO to turn ON heater
}
}
